# Fritzing sketch AutoBadger (saved by Fritzing 0.9.5d)

parts:
  Part1 = Arduino Uno (Rev3)
  Servo = Basic Servo
  KY-1 = Keyes Relay [package=THT]
  Strobe = smd LED [color="Red (633nm)" package="1206 [SMD]"]
  S1 = Square Pushbutton

nets:
  GND: Part1.GND, Servo.gnd, KY-1.ground, S1.leg0
  N1: Part1.D2, Servo.pulse
  N2: Part1.D3_PWM, KY-1.signal
  N3: Part1.D4, S1.leg1
  3V3: Part1.3V3, Servo.vcc
  N4: Part1.5V, KY-1.power
  N5: KY-1.NO, Strobe.anode

notes:
  Connect to power, either 12V, 24V, or 220V depending on what strobe you have. Check that beforehand!
  You'll also need to power the Arduino board, either via USB or external power supply.

custom parts:
  Keyes Relay: The Keyes 5V relay module is suitable for SCM development, home appliance control. It uses a 5V~12V TIL control signal which can control DC / AC signal.
